# Fritzing sketch circuit_diagram (saved by Fritzing 0.9.3b)
breadboards: 1

parts:
  Raspberry_Pi1 = Raspberry Pi B rev2
  C1 = Ceramic Capacitor [capacitance=0.1µF package="100 mil [THT, multilayer]"]
  R1 = Resistor [tolerance=±5% resistance=1k package=THT]
  IR_sensor = mystery part, 3 pins [chip_label=IR]
  R2 = Resistor [tolerance=±5% resistance=1k package=THT]

nets:
  N1: Raspberry_Pi1.3V3, R1.Pin_0
  N2: Raspberry_Pi1.GPIO_4, IR_sensor.pin1
  N3: Raspberry_Pi1.GND, C1.0, IR_sensor.pin2
  N4: C1.1, IR_sensor.pin3, R2.Pin_1
  N5: R1.Pin_1, R2.Pin_0
